# Fritzing sketch Esquema_Conexiones (saved by Fritzing 0.9.3b)
breadboards: 1

parts:
  LEDlm = smd LED [color="Yellow (595nm)" package="1206 [SMD]"]
  LED2 = smd LED [color="Blue (430nm)" package="1206 [SMD]"]
  LED3 = smd LED [color="Red (633nm)" package="1206 [SMD]"]
  LED4 = smd LED [color="Red (635nm)" package="1206 [SMD]"]
  LED5 = smd LED [color="Green (570nm)" package="1206 [SMD]"]
  LED6 = smd LED [color="Green (570nm)" package="1206 [SMD]"]
  LED7 = smd LED [color="Yellow (595nm)" package="1206 [SMD]"]
  LED8 = smd LED [color="Blue (470nm)" package="1206 [SMD]"]
  R1 = Resistor [tolerance=±5% resistance=220 package=THT]
  R2 = Resistor [tolerance=±5% resistance=220 package=THT]
  R3 = Resistor [tolerance=±5% resistance=220 package=THT]
  R4 = Resistor [tolerance=±5% resistance=220 package=THT]
  R5 = Resistor [tolerance=±5% resistance=220 package=THT]
  R6 = Resistor [tolerance=±5% resistance=220 package=THT]
  R7 = Resistor [tolerance=±5% resistance=220 package=THT]
  R8 = Resistor [tolerance=±5% resistance=220 package=THT]
  J1 = Basic Servo
  Componente2 = HC-SR04
  DHT1 = DHT11 Humitidy and Temperature Sensor
  IR_Sensor_Switch1 = Infrared Sensor Switch
  LED1 = smd LED [color="Blue (430nm)" package="1206 [SMD]"]
  T1 = LM35 Temperature Sensor [package="TO92 [THT]"]
  Componente1 = Arduino Mega ADK (Rev3)

nets (from the schematic view):
  GND: LEDlm.cathode, LED2.anode, LED3.cathode, LED4.cathode, LED5.cathode, LED7.cathode, LED8.anode, R4.Pin_0, R6.Pin_0, R7.Pin_0, R8.Pin_0, J1.gnd, Componente2.Gnd, DHT1.GND, IR_Sensor_Switch1.GND, T1.GND, Componente1.GND
  N1: LED2.cathode, R2.Pin_0
  N2: LED6.cathode, R5.Pin_0, Componente1.3V3
  N3: LED8.cathode, R3.Pin_0, R3.Pin_1, Componente1.D9_PWM
  N4: R1.Pin_0, LED1.cathode
  N5: R1.Pin_1, Componente1.D13_PWM
  N6: R2.Pin_1, Componente1.D12_PWM
  N7: R4.Pin_1, Componente1.D11_PWM
  N8: R5.Pin_1, Componente1.D8_PWM
  N9: R6.Pin_1, Componente2.Trig, Componente1.D5_PWM
  N10: R7.Pin_1, Componente1.D4_PWM
  N11: R8.Pin_1, Componente1.D2_PWM
  VCC: J1.vcc, IR_Sensor_Switch1.Vcc, T1.+Vs
  VCC_2: Componente2.Vcc, DHT1.VDD, Componente1.5V
  N12: Componente2.Echo, Componente1.D6_PWM
  N13: DHT1.DATA, Componente1.D3_PWM
  N14: IR_Sensor_Switch1.OUT, Componente1.D16/TX2
  N15: T1.Vout, Componente1.A0

custom parts:
  HC-SR04: HC-SR04 ultrasonic distance sensor
  DHT11 Humitidy and Temperature Sensor: DHT11 Humidity and Temperature Sensor
  Infrared Sensor Switch: - Working voltage: DC 5V - Working current: 10~15mA - Detecting range: 3~80cm (adjustable) - Red: VCC, Green: GND, Yellow: OUT
